// Logisim project 4 BIT MAGNITUDE COMPARATOR.circ as structural Verilog: 1 circuit, main circuit main
module main (
  input  A3,
  input  B3,
  input  A2,
  input  B2,
  input  A1,
  input  B1,
  input  A0,
  input  B0,
  input  A3_2,
  input  B3_2,
  input  A2_2,
  input  B2_2,
  input  A1_2,
  input  B1_2,
  input  in_15,
  input  A0_2,
  output A___B,
  output out_18
);

  wire and_1_out, and_2_out, and_3_out, and_4_out, xnor_1_out, xnor_2_out, xnor_3_out;

  xnor xnor_1 (xnor_1_out, A3, B3);
  xnor xnor_2 (xnor_2_out, A2, B2);
  xnor xnor_3 (xnor_3_out, A1, B1);
  xnor xnor_4 (xnor_3_out, A0, B0);
  and and_1 (and_1_out, A3_2, B3_2);
  and and_2 (and_2_out, A2_2, B2_2, xnor_1_out);
  and and_3 (and_3_out, A1_2, B1_2, xnor_1_out, xnor_1_out);
  and and_4 (and_4_out, in_15, A0_2, xnor_1_out, xnor_1_out, xnor_1_out);
  and and_5 (A___B, xnor_1_out, xnor_2_out, xnor_3_out, xnor_3_out);
  or or_1 (out_18, and_1_out, and_2_out, and_3_out, and_4_out);
endmodule
